# Fritzing sketch lcd-crystal-ball (saved by Fritzing 0.9.4)
breadboards: 1

parts:
  Part1 = Arduino Uno (Rev3)
  R1 = Resistor [tolerance=±5% resistance=220 package=THT]
  S1 = TILT-SWITCH-SW-200D [package=reed_switch_plastic]
  R2 = Resistor [tolerance=±5% resistance=10k package=THT]
  R3 = Rotary Potentiometer (Small) [maximum_resistance=100kΩ package=THT]
  LCD1 = LCD screen

nets:
  N1: Part1.D11_PWM/MOSI, LCD1.E
  N2: Part1.D12/MISO, LCD1.RS
  N3: Part1.D2, LCD1.DB7
  N4: Part1.D3_PWM, LCD1.DB6
  N5: Part1.D4, LCD1.DB5
  N6: Part1.D5_PWM, LCD1.DB4
  N7: Part1.D6_PWM, S1.2, R2.Pin_1
  5V: Part1.5V, R1.Pin_1, R3.leg1, LCD1.VDD
  GND: Part1.GND, S1.1, R2.Pin_0, R3.leg2, LCD1.VSS, LCD1.R/W, LCD1.LED-
  N8: R1.Pin_0, LCD1.LED+
  N9: R3.wiper, LCD1.V0
