# Fritzing sketch led-button-parallel-1 (saved by Fritzing 0.9.4)
breadboards: 1

parts:
  Part1 = Arduino Uno (Rev3)
  R1 = Resistor [tolerance=±5% resistance=220 package=THT]
  LED1 = LED - 5mm [color="Red (633nm)" package="5 mm [THT]"]
  S1 = Pushbutton [package=THT]
  S2 = Pushbutton [package=THT]

nets:
  N1: Part1.GND, R1.Pin_1, LED1.cathode
  N2: R1.Pin_0, S1.leg1, S2.leg1
  N3: LED1.anode, S1.leg0, S2.leg0
