# Fritzing sketch led-button-series-2 (saved by Fritzing 0.9.4)
breadboards: 1

parts:
  Part1 = Arduino Uno (Rev3)
  R1 = Resistor [tolerance=±5% resistance=220 package=THT]
  LED1 = LED - 5mm [color="Red (633nm)" package="5 mm [THT]"]
  S1 = Pushbutton [package=THT]
  S2 = Pushbutton [package=THT]
  S3 = Pushbutton [package=THT]

nets (from the breadboard view):
  N1: Part1.5V, LED1.cathode
  N2: Part1.GND, R1.Pin_1
  N3: R1.Pin_0, S1.leg1
  N4: LED1.anode, S3.leg0
  N5: S1.leg0, S2.leg1
  N6: S2.leg0, S3.leg1
