# Fritzing sketch led-rgb (saved by Fritzing 0.9.4)
breadboards: 1

parts:
  Part1 = Arduino Uno (Rev3)
  R1 = Resistor [tolerance=±5% resistance=220 package=THT]
  R2 = Resistor [tolerance=±5% resistance=220 package=THT]
  R3 = Resistor [tolerance=±5% resistance=220 package=THT]
  LED3 = RGB LED (com. anode, rbg) [package="5 mm [THT]"]
  R4 = Photocell (LDR) [package=THT]
  R5 = Photocell (LDR) [package=THT]
  R6 = Photocell (LDR) [package=THT]
  R7 = Resistor [tolerance=±5% resistance=10k package="1206 [SMD]"]
  R8 = Resistor [tolerance=±5% resistance=10k package="1206 [SMD]"]
  R9 = Resistor [tolerance=±5% resistance=10k package="1206 [SMD]"]

nets:
  N1: Part1.A0, Part1.A1, Part1.A2, Part1.5V, R4.pin_0, R5.pin_0, R6.pin_0, R7.Pin_0, R8.Pin_0, R9.Pin_0
  N2: Part1.D9_PWM, R3.Pin_0
  N3: Part1.D10_PWM/SS, R2.Pin_0
  N4: Part1.D11_PWM/MOSI, R1.Pin_0
  N5: Part1.GND, LED3.common_anode
  N6: R1.Pin_1, LED3.red_cathode
  N7: R2.Pin_1, LED3.blue_cathode
  N8: R3.Pin_1, LED3.green_cathode
  N9: R4.pin_1, R7.Pin_1
  N10: R5.pin_1, R8.Pin_1
  N11: R6.pin_1, R9.Pin_1
