# Fritzing sketch piezo-resistor-ladder (saved by Fritzing 0.9.4)
breadboards: 1

parts:
  Part1 = Arduino Uno (Rev3)
  R1 = Resistor [tolerance=±5% resistance=220 package=THT]
  R2 = Resistor [tolerance=±5% resistance=10k package=THT]
  R3 = Resistor [tolerance=±5% resistance=1M package=THT]
  J1 = Piezo Speaker
  S1 = Pushbutton [package="[SMD]"]
  S2 = Pushbutton [package="[SMD]"]
  S3 = Pushbutton [package="[SMD]"]
  S4 = Pushbutton [package="[SMD]"]
  R4 = Resistor [tolerance=±5% resistance=10 package=THT]

nets:
  N1: Part1.A0, Part1.GND, J1.pin1, S1.Pin_1, S1.Pin_2, S2.Pin_1, S2.Pin_2, S3.Pin_1, S3.Pin_2, S4.Pin_1, S4.Pin_2, R4.Pin_1
  N2: Part1.D8, J1.pin2
  N3: Part1.5V, R1.Pin_1, R2.Pin_1, R3.Pin_1, S1.Pin_3, S1.Pin_4
  N4: R1.Pin_0, S2.Pin_3, S2.Pin_4
  N5: R2.Pin_0, S3.Pin_3, S3.Pin_4
  N6: R3.Pin_0, S4.Pin_3, S4.Pin_4
