# Fritzing sketch button-reset (saved by Fritzing 0.9.4)
breadboards: 1

parts:
  R1 = Resistor [tolerance=±5% resistance=10k package=THT]
  S1 = Pushbutton [package="[THT]"]
  Part1 = Arduino Uno (Rev3) - ICSP

nets:
  N1: R1.Pin_0, S1.Pin_3, S1.Pin_4, Part1.GND
  N2: R1.Pin_1, S1.Pin_1, S1.Pin_2, Part1.RESET
