# Fritzing sketch temt6000 (saved by Fritzing 0.9.3b)

parts:
  Part1 = Arduino Uno (Rev3)
  Part2 = Ambient Light Sensor (TEMT6000 Breakout Board)

nets:
  N1: Part1.A0, Part2.S
  5V: Part1.5V, Part2.VCC
  GND: Part1.GND, Part2.GND
