# Fritzing sketch ds18b20 (saved by Fritzing 0.9.3b)

parts:
  Part1 = Arduino Uno (Rev3)
  DS1 = DS18B20 1-Wire Temperature Sensor [part_number=DS18B20]

nets:
  N1: Part1.D10_PWM/SS, DS1.DQ
  3V3: Part1.3V3, DS1.VDD
  GND: Part1.GND, DS1.GND
