# Fritzing sketch hbridge-motor (saved by Fritzing 0.9.4)
breadboards: 1

parts:
  Part1 = Arduino Uno (Rev3)
  S1 = Pushbutton [package="[SMD]"]
  VCC1 = Battery block 9V
  S2 = Pushbutton [package="[SMD]"]
  U1 = POT [package=pot_alpha_rv16af-20]
  M1 = DC Motor
  IC1 = L293D [package=THT]
  R1 = Resistor [tolerance=±5% resistance=10k package="1206 [SMD]"]
  R2 = Resistor [tolerance=±5% resistance=10k package="1206 [SMD]"]

nets:
  N1: Part1.A0, U1.S
  N2: Part1.D9_PWM, IC1.Enable_1
  N3: Part1.D2, IC1.In_2
  N4: Part1.D3_PWM, IC1.In_1
  N5: Part1.D4, S2.Pin_1, S2.Pin_2, R2.Pin_1
  N6: Part1.D5_PWM, S1.Pin_1, S1.Pin_2, R1.Pin_1
  N7: Part1.5V, S1.Pin_3, S1.Pin_4, S2.Pin_3, S2.Pin_4, U1.A, IC1.+V
  N8: Part1.GND, VCC1.-, U1.E, IC1.0V, R1.Pin_0, R2.Pin_0
  N9: VCC1.+, IC1.+Vmotor
  N10: M1.pin_1, IC1.Out_2_(_Controlled_by_Enable_1_)
  N11: M1.pin_2, IC1.Out_1_(_Controlled_by_Enable_1_)
