# Fritzing sketch motor-button (saved by Fritzing 0.9.4)
breadboards: 1

parts:
  Part1 = Arduino Uno (Rev3)
  S1 = Pushbutton [package="[SMD]"]
  R1 = Resistor [tolerance=±5% resistance=10k package=THT]
  Q1 = Basic FET P-Channel [package="D2Pak [SMD]"]
  VCC1 = Battery block 9V
  M1 = DC Motor
  D1 = Diode [package=diode-hv]

nets:
  N1: Part1.D9_PWM, Q1.Gate
  N2: Part1.D2, S1.Pin_1, S1.Pin_2, R1.Pin_0
  N3: Part1.5V, S1.Pin_3, S1.Pin_4
  N4: Part1.GND, R1.Pin_1, Q1.source
  N5: Q1.drain, M1.pin_2
  N6: VCC1.+, M1.pin_1, D1.C
