# Fritzing sketch servo-pot (saved by Fritzing 0.9.4)
breadboards: 1

parts:
  Part1 = Arduino Uno (Rev3)
  J1 = Basic Servo
  U1 = POT [package=alps_pot]
  C1 = Capacitor Polarized [package=panasonic_e]
  C2 = Capacitor Polarized [package=panasonic_e]

nets:
  N1: Part1.A0, U1.S
  GND: Part1.D9_PWM, Part1.GND, J1.gnd, J1.pulse, U1.A, C1.-, C2.+
  5V: Part1.5V, J1.vcc, U1.E, C1.+, C2.-
